# Fritzing sketch FuelCellBoard_v2 (saved by Fritzing 0.9.4)
circuit board: 4.85296cm x 8.05296cm
breadboards: 1

parts:
  DFRobot_DFPlayer_Mini1 = DFRobot DFPlayer Mini [part_number=DFR0299]
  R1 = Resistor [tolerance=±5% resistance=10 package=THT]
  Speaker = female pin header, 3 pins [form="♀ (female)"]
  Arduino_Micro = Arduino Micro (Rev3)
  Vol = Trimmer Potentiometer [maximum_resistance=100kΩ package=THT]
  Power_VIN = female pin header, 4 pins [form="♀ (female)"]
  Output = female pin header, 4 pins [form="♀ (female)"]
  Power_5v = female pin header, 4 pins [form="♀ (female)"]
  Output_LED1 = female pin header, 3 pins [form="♀ (female)"]
  GND = female pin header, 2 pins [form="♀ (female)"]
  Input = molex pin header, 4 pins [form=molex]
  R11 = Resistor [tolerance=±5% resistance=220 package=THT]
  R12 = Resistor [tolerance=±5% resistance=220 package=THT]
  R13 = Resistor [tolerance=±5% resistance=220 package=THT]
  R4 = Resistor [tolerance=±5% resistance=220 package=THT]
  R14 = Resistor [tolerance=±5% resistance=220 package=THT]
  R15 = Resistor [tolerance=±5% resistance=220 package=THT]
  R16 = Resistor [tolerance=±5% resistance=220 package=THT]

nets:
  VCC: DFRobot_DFPlayer_Mini1.VCC, Arduino_Micro.5V, Vol.leg2, Power_5v.pin1, Power_5v.pin2
  N1: DFRobot_DFPlayer_Mini1.RX, R1.Pin_1
  N2: DFRobot_DFPlayer_Mini1.TX, Arduino_Micro.D10_PWM/A10
  N3: DFRobot_DFPlayer_Mini1.SPK_1, Speaker.pin1
  N4: DFRobot_DFPlayer_Mini1.GND-1, DFRobot_DFPlayer_Mini1.GND-2, Speaker.pin2, Arduino_Micro.GND, Vol.leg1, Power_VIN.pin1, Power_VIN.pin2, Power_5v.pin3, Power_5v.pin4, GND.pin1, GND.pin2, R11.Pin_1, R12.Pin_1, R13.Pin_1, R4.Pin_1
  N5: DFRobot_DFPlayer_Mini1.SPK_2, Speaker.pin3
  N6: R1.Pin_0, Arduino_Micro.D11_PWM
  N7: Arduino_Micro.D2/SDA, R16.Pin_0
  N8: Arduino_Micro.D3/SCL, R15.Pin_0
  N9: Arduino_Micro.D4_PWM/A6, R14.Pin_0
  N10: Arduino_Micro.D5_PWM, Output.pin4
  N11: Arduino_Micro.D6_PWM/A7, Output.pin3
  N12: Arduino_Micro.D7, Output.pin2
  N13: Arduino_Micro.D12_PWM/A11, Output.pin1
  N14: Arduino_Micro.VIN, Power_VIN.pin3, Power_VIN.pin4
  N15: Arduino_Micro.A5, Vol.wiper
  N16: Arduino_Micro.A3, Input.pin4, R4.Pin_0
  N17: Arduino_Micro.A2, Input.pin3, R13.Pin_0
  N18: Arduino_Micro.A1, Input.pin2, R12.Pin_0
  N19: Arduino_Micro.A0, Input.pin1, R11.Pin_0
  N20: Output_LED1.pin1, R14.Pin_1
  N21: Output_LED1.pin2, R15.Pin_1
  N22: Output_LED1.pin3, R16.Pin_1

notes:
  -
  +
